# Fritzing sketch Bai 1 (saved by Fritzing 0.9.3b)
breadboards: 1

parts:
  ESP32_DevKit_V1 = DOIT Esp32 DevKit v1 (30 pins long, 11 pins width) [part_number=ESP32S-PIN30]
  R1_330_ohm = Resistor [resistance=330 package=THT]
  LED1 = Red LED - 5mm [package="5 mm [THT]"]
  SW1_GPIO4 = Pushbutton [package="[THT]"]

nets:
  N1: ESP32_DevKit_V1.GND, LED1.cathode, SW1_GPIO4.Pin_1, SW1_GPIO4.Pin_2
  N2: ESP32_DevKit_V1.D2, R1_330_ohm.Pin_0
  N3: ESP32_DevKit_V1.D4, SW1_GPIO4.Pin_3, SW1_GPIO4.Pin_4
  N4: R1_330_ohm.Pin_1, LED1.anode

custom parts:
  DOIT Esp32 DevKit v1 (30 pins long, 11 pins width): The DOIT Esp32 DevKit v1 is one of the development board created by DOIT to evaluate the ESP-WROOM-32 module. It is based on the ESP32 microcontroller that boasts Wifi, Bluetooth, Ethernet and Low Power support all in a single chip. (vanepp) made breadboard work, adjusted pin numbering and labels and reduced size of schematic and cleaned up pcb. This chip is 30pins long (2 x15) and 11 pins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
  330 ohm Resistor: A generic resistor (0.25W)
  Red LED - 5mm: A generic red LED (~1.8V)
  Pushbutton: A generic pushbutton.

// code stored in the sketch: Untitled3.ino
#include <Arduino.h>
#define LED_GPIO 2
#include "pwm_compat.h"
#ifndef USE_INTERRUPT
#define USE_INTERRUPT 0
#endif
constexpr int BUTTON_PIN = 4;
portMUX_TYPE mux = portMUX_INITIALIZER_UNLOCKED;
volatile uint32_t edgeCount = 0;
void IRAM_ATTR onButton() {
  portENTER_CRITICAL_ISR(&mux);
  ++edgeCount;
  portEXIT_CRITICAL_ISR(&mux);
}
uint32_t count = 0;
bool previousLow = false;
int brightness = 0, direction = 1;
uint32_t lastStep = 0, flashStart = 0;
bool flashing = false;
void signalPress(uint32_t n) {
  count += n;
  Serial.printf("mode:%s count:%lu edges:%lu\n", USE_INTERRUPT ? "interrupt" : "polling",
                (unsigned long)count, (unsigned long)n);
  flashStart = millis(); flashing = true;
}
void setup() {
  Serial.begin(115200);
  pinMode(BUTTON_PIN, INPUT_PULLUP);
  pwmBegin();
#if USE_INTERRUPT
  attachInterrupt(digitalPinToInterrupt(BUTTON_PIN), onButton, FALLING);
#endif
  Serial.println(USE_INTERRUPT ? "INTERRUPT (no debounce)" : "POLLING every 10 ms (no debounce)");
}
void loop() {
#if USE_INTERRUPT
  portENTER_CRITICAL(&mux);
  uint32_t n = edgeCount; edgeCount = 0;
  portEXIT_CRITICAL(&mux);
  if (n) signalPress(n);
#else
  bool low = digitalRead(BUTTON_PIN) == LOW;
  if (low && !previousLow) signalPress(1);
  previousLow = low;
#endif
  uint32_t now = millis();
  if (now - lastStep >= 10) {
    lastStep = now;
    brightness += direction;
    if (brightness == 255 || brightness == 0) direction = -direction;
  }
  if (flashing && now - flashStart >= 160) flashing = false;
  pwmWrite(flashing ? (now - flashStart < 80 ? 0 : 255) : brightness);
  // Both versions use the same workload. An ISR captures edges during this delay.
  delay(10);
}
