# Fritzing sketch Bai 3 (saved by Fritzing 0.9.3b)
breadboards: 1

parts:
  ESP32_DevKit_V1 = DOIT Esp32 DevKit v1 (30 pins long, 11 pins width) [part_number=ESP32S-PIN30]
  R1_330_ohm = Resistor [resistance=330 package=THT]
  LED1 = Red LED - 5mm [package="5 mm [THT]"]
  RV1_10k_ohm = 10k ohm Rotary Potentiometer [maximum_resistance=10kΩ package=THT]

nets:
  N1: ESP32_DevKit_V1.3V3, RV1_10k_ohm.leg1
  N2: ESP32_DevKit_V1.GND, LED1.cathode, RV1_10k_ohm.leg2
  N3: ESP32_DevKit_V1.D18, R1_330_ohm.Pin_0
  N4: ESP32_DevKit_V1.D34, RV1_10k_ohm.wiper
  N5: R1_330_ohm.Pin_1, LED1.anode

custom parts:
  DOIT Esp32 DevKit v1 (30 pins long, 11 pins width): The DOIT Esp32 DevKit v1 is one of the development board created by DOIT to evaluate the ESP-WROOM-32 module. It is based on the ESP32 microcontroller that boasts Wifi, Bluetooth, Ethernet and Low Power support all in a single chip. (vanepp) made breadboard work, adjusted pin numbering and labels and reduced size of schematic and cleaned up pcb. This chip is 30pins long (2 x15) and 11 pins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
  330 ohm Resistor: A generic resistor (0.25W)
  Red LED - 5mm: A generic red LED (~1.8V)
  10k ohm Rotary Potentiometer: A rotary adjustable resistor (potentiometer).
